// Logisim project PIP2.0.circ as structural Verilog: 15 circuits, main circuit Register_File
// Regiser_File
module Register_File (
  input  [2:0] RA,
  input  [2:0] RB,
  input  [2:0] RW,
  input  [15:0] BusW,
  input  Reg_Write,
  input  clk,
  output [15:0] r1,
  output [15:0] r2,
  output [15:0] BusA,
  output [15:0] r3,
  output [15:0] r4,
  output [15:0] BusB,
  output [15:0] r5,
  output [15:0] r6,
  output [15:0] r7
);

  wire A_D0, A_D1, A_D2, A_D3, A_D4, A_D5, A_D6, A_D7, and_1_out, and_2_out, and_3_out, and_4_out, and_5_out,
       and_6_out, and_7_out, B_D0, B_D1, B_D2, B_D3, B_D4, B_D5, B_D6, B_D7, R1_Enable, R2_Enable, R3_Enable,
       R4_Enable, R5_Enable, R6_Enable, R7_Enable;
  wire [15:0] R1_q;

  Decoder #(.select(3), .enable("false")) decoder_1 (
    .out1(R1_Enable), .out2(R2_Enable), .out3(R3_Enable), .out4(R4_Enable), .out5(R5_Enable),
    .out6(R6_Enable), .out7(R7_Enable), .sel(RW));  // open: out0
  Decoder #(.select(3), .enable("false")) decoder_2 (
    .out0(A_D0), .out1(A_D1), .out2(A_D2), .out3(A_D3), .out4(A_D4), .out5(A_D5), .out6(A_D6), .out7(A_D7),
    .sel(RA));
  Decoder #(.select(3), .enable("false")) decoder_3 (
    .out0(B_D0), .out1(B_D1), .out2(B_D2), .out3(B_D3), .out4(B_D4), .out5(B_D5), .out6(B_D6), .out7(B_D7),
    .sel(RB));
  and and_1 (and_1_out, Reg_Write, R1_Enable);
  and and_2 (and_2_out, Reg_Write, R2_Enable);
  and and_3 (and_3_out, Reg_Write, R3_Enable);
  and and_4 (and_4_out, Reg_Write, R4_Enable);
  and and_5 (and_5_out, Reg_Write, R5_Enable);
  and and_6 (and_6_out, Reg_Write, R6_Enable);
  and and_7 (and_7_out, Reg_Write, R7_Enable);
  Register #(.width(16)) u_R1 (.D({16{1'b0}}), .Q(R1_q), .clk(clk));  // open: en, clr
  Register #(.width(16)) R1_2 (.D(BusW), .en(and_1_out), .Q(r1), .clk(clk));  // open: clr
  Register #(.width(16)) u_R2 (.D(BusW), .en(and_2_out), .Q(r2), .clk(clk));  // open: clr
  Register #(.width(16)) u_R3 (.D(BusW), .en(and_3_out), .Q(r3), .clk(clk));  // open: clr
  Register #(.width(16)) u_R4 (.D(BusW), .en(and_4_out), .Q(r4), .clk(clk));  // open: clr
  Register #(.width(16)) u_R5 (.D(BusW), .en(and_5_out), .Q(r5), .clk(clk));  // open: clr
  Register #(.width(16)) u_R6 (.D(BusW), .en(and_6_out), .Q(r6), .clk(clk));  // open: clr
  Register #(.width(16)) u_R7 (.D(BusW), .en(and_7_out), .Q(r7), .clk(clk));  // open: clr
  assign BusB = B_D0 ? R1_q : 16'bz;  // Controlled_Buffer controlled_buffer_1
  assign BusB = B_D1 ? r1 : 16'bz;  // Controlled_Buffer controlled_buffer_2
  assign BusB = B_D2 ? r2 : 16'bz;  // Controlled_Buffer controlled_buffer_3
  assign BusB = B_D3 ? r3 : 16'bz;  // Controlled_Buffer controlled_buffer_4
  assign BusB = B_D4 ? r4 : 16'bz;  // Controlled_Buffer controlled_buffer_5
  assign BusB = B_D5 ? r5 : 16'bz;  // Controlled_Buffer controlled_buffer_6
  assign BusB = B_D6 ? r6 : 16'bz;  // Controlled_Buffer controlled_buffer_7
  assign BusB = B_D7 ? r7 : 16'bz;  // Controlled_Buffer controlled_buffer_8
  assign BusA = A_D0 ? R1_q : 16'bz;  // Controlled_Buffer controlled_buffer_9
  assign BusA = A_D1 ? r1 : 16'bz;  // Controlled_Buffer controlled_buffer_10
  assign BusA = A_D2 ? r2 : 16'bz;  // Controlled_Buffer controlled_buffer_11
  assign BusA = A_D3 ? r3 : 16'bz;  // Controlled_Buffer controlled_buffer_12
  assign BusA = A_D4 ? r4 : 16'bz;  // Controlled_Buffer controlled_buffer_13
  assign BusA = A_D5 ? r5 : 16'bz;  // Controlled_Buffer controlled_buffer_14
  assign BusA = A_D6 ? r6 : 16'bz;  // Controlled_Buffer controlled_buffer_15
  assign BusA = A_D7 ? r7 : 16'bz;  // Controlled_Buffer controlled_buffer_16
endmodule

module ALU (
  input  [15:0] A,
  input  [15:0] B,
  input  [2:0] ALU_Function,
  input  ALU_Select,
  output ZERO,
  output [15:0] ALU_Output
);

  wire [15:0] au_1_arithmetic_output, lu_and_shifter_1_opcode0_output, nor_1_out;

  LU_and_Shifter lu_and_shifter_1 (
    .Opcode0_Output(lu_and_shifter_1_opcode0_output), .A(A), .B(B), .Opcode0_Select(ALU_Function));
  AU au_1 (.Arithmetic_Output(au_1_arithmetic_output), .A(A), .B(B), .Arithmetic_Select(ALU_Function));
  Multiplexer #(.width(16), .enable("false")) multiplexer_1 (
    .in0(lu_and_shifter_1_opcode0_output), .in1(au_1_arithmetic_output), .out(ALU_Output), .sel(ALU_Select));
  assign {{8{nor_1_out[15]}}, nor_1_out[7:0]} = ~(ALU_Output | ALU_Output);  // NOR_Gate nor_1, 16 bits wide
  and and_1 (ZERO, nor_1_out[0], nor_1_out[1], nor_1_out[2], nor_1_out[3], nor_1_out[4], nor_1_out[5], nor_1_out[6], nor_1_out[7], nor_1_out[15], nor_1_out[15], nor_1_out[15], nor_1_out[15], nor_1_out[15], nor_1_out[15], nor_1_out[15], nor_1_out[15]);
endmodule

module Logical_Unit (
  input  [15:0] A,
  input  [15:0] B,
  output [15:0] AND_Output,
  output [15:0] OR_Output,
  output [15:0] NOR_Output,
  output [15:0] XOR_Output
);

  assign AND_Output = B & A;  // AND_Gate AND, 16 bits wide
  assign OR_Output = B | A;  // OR_Gate OR, 16 bits wide
  assign XOR_Output = B ^ A;  // XOR_Gate XOR, 16 bits wide
  assign NOR_Output = ~OR_Output;  // NOT_Gate not_1, 16 bits wide
endmodule

module Shifter (
  input  [3:0] Shift_Amount,
  input  [15:0] Number,
  output [15:0] SLL_Output,
  output [15:0] SRL_Output,
  output [15:0] SRA_Output,
  output [15:0] ROL_Output
);

  Shifter_part #(.width(16)) shifter_1 (.in(Number), .\dist (Shift_Amount), .out(SLL_Output));
  Shifter_part #(.width(16), .shift("lr")) shifter_2 (.in(Number), .\dist (Shift_Amount), .out(SRL_Output));
  Shifter_part #(.width(16), .shift("ar")) shifter_3 (.in(Number), .\dist (Shift_Amount), .out(SRA_Output));
  Shifter_part #(.width(16), .shift("rl")) shifter_4 (.in(Number), .\dist (Shift_Amount), .out(ROL_Output));
endmodule

module AU (
  input  [15:0] A,
  input  [15:0] B,
  input  [2:0] Arithmetic_Select,
  output [15:0] Arithmetic_Output
);

  wire subtractor_1_bout, subtractor_2_bout, xor_1_out;
  wire [15:0] Add_Output, Different_sign_Comp, nor_1_out, or_1_out, or_2_out, SLT, SLTE, SLTEU, SLTU,
       Sub_Output;

  xor xor_1 (xor_1_out, A[15], B[15]);
  Adder #(.width(16)) adder_1 (.a(A), .b(B), .out(Add_Output));  // open: cin, cout
  Subtractor #(.width(16)) subtractor_1 (.a(A), .b(B), .out(Sub_Output), .bout(subtractor_1_bout));  // open: bin
  Subtractor #(.width(1)) subtractor_2 (.a(B[15]), .b(A[15]), .bout(subtractor_2_bout));  // open: out, bin
  assign SLTU = {{15{1'b0}}, subtractor_1_bout};  // Bit_Extender bit_extender_1
  Multiplexer #(.width(16), .enable("false")) multiplexer_1 (
    .in0(SLTU), .in1(Different_sign_Comp), .out(SLT), .sel(xor_1_out));
  assign Different_sign_Comp = {{15{1'b0}}, subtractor_2_bout};  // Bit_Extender bit_extender_2
  assign nor_1_out = ~({16{1'b0}} | Sub_Output);  // NOR_Gate nor_1, 16 bits wide
  assign or_1_out = SLTU | nor_1_out;  // OR_Gate or_1, 16 bits wide
  assign or_2_out = nor_1_out | SLT;  // OR_Gate or_2, 16 bits wide
  assign SLTEU = {{15{1'b0}}, or_1_out[0]};  // Bit_Extender bit_extender_3
  assign SLTE = {{15{1'b0}}, or_2_out[0]};  // Bit_Extender bit_extender_4
  Multiplexer #(.select(3), .width(16), .enable("false")) multiplexer_2 (
    .in0(Add_Output), .in1(Sub_Output), .in2(SLT), .in3(SLTU), .in4(SLTE), .in5(SLTEU),
    .out(Arithmetic_Output), .sel(Arithmetic_Select));  // open: in6, in7
endmodule

// LU&Shifter
module LU_and_Shifter (
  input  [15:0] A,
  input  [15:0] B,
  input  [2:0] Opcode0_Select,
  output [15:0] Opcode0_Output
);

  wire [15:0] logical_unit_1_and_output, logical_unit_1_nor_output, logical_unit_1_or_output,
       logical_unit_1_xor_output, shifter_1_rol_output, shifter_1_sll_output, shifter_1_sra_output,
       shifter_1_srl_output;

  Logical_Unit logical_unit_1 (
    .B(B), .A(A), .AND_Output(logical_unit_1_and_output), .OR_Output(logical_unit_1_or_output),
    .NOR_Output(logical_unit_1_nor_output), .XOR_Output(logical_unit_1_xor_output));
  Shifter shifter_1 (
    .Shift_Amount(B[3:0]), .Number(A), .SLL_Output(shifter_1_sll_output), .SRL_Output(shifter_1_srl_output),
    .SRA_Output(shifter_1_sra_output), .ROL_Output(shifter_1_rol_output));
  Multiplexer #(.select(3), .width(16), .enable("false")) multiplexer_1 (
    .in0(logical_unit_1_and_output), .in1(logical_unit_1_or_output), .in2(logical_unit_1_nor_output),
    .in3(logical_unit_1_xor_output), .in4(shifter_1_sll_output), .in5(shifter_1_srl_output),
    .in6(shifter_1_sra_output), .in7(shifter_1_rol_output), .out(Opcode0_Output), .sel(Opcode0_Select));
endmodule

module Main_Controller (
  input  [2:0] Function,
  input  [3:0] Opcode,
  input  Stall,
  output [2:0] Function_Output,
  output JR,
  output Reg_Dst,
  output Reg_Write,
  output Ext_Op,
  output ALU_Src,
  output BEQ,
  output BNE,
  output BGTZ,
  output BLTZ,
  output Mem_Read,
  output Mem_Write,
  output Mem_to_Reg,
  output ALU_Select,
  output LUI,
  output JAL,
  output J,
  output Write_Select,
  output BusW_imm
);

  wire ADDI, ANDI, BEQ_t, BGEZ, BGTZ_t, BLEZ, BLTZ_t, J_t, JAL_t, JALR, nor_1_out, not_1_out, or_12_out, ORI,
       Rtype0000, Rtype0001;
  wire [2:0] bit_extender_1_out, multiplexer_1_out;

  Decoder #(.select(4)) decoder_1 (
    .out0(Rtype0000), .out1(Rtype0001), .out2(Mem_Read), .out3(Mem_Write), .out4(BEQ_t), .out5(BNE),
    .out6(ANDI), .out7(ORI), .out8(ADDI), .out9(J_t), .out10(LUI), .out11(JAL_t), .out12(BLTZ_t),
    .out13(BLEZ), .out14(BGTZ_t), .out15(BGEZ), .sel(Opcode), .en(not_1_out));
  not not_1 (not_1_out, Stall);
  or or_1 (Reg_Dst, Rtype0000, Rtype0001);
  or or_2 (Reg_Write, Rtype0000, Rtype0001, Mem_Read, ANDI, ORI, ADDI, JAL_t, LUI);
  or or_3 (Ext_Op, Mem_Read, Mem_Write, ADDI);
  or or_4 (ALU_Src, Mem_Read, Mem_Write, ANDI, ORI, ADDI);
  or or_5 (BEQ, BEQ_t, BLEZ, BGEZ);
  or or_6 (BGTZ, BGEZ, BGTZ_t);
  or or_7 (BLTZ, BLEZ, BLTZ_t);
  or or_8 (ALU_Select, BGEZ, BGTZ_t, BLEZ, BLTZ_t, Rtype0001, Mem_Read, Mem_Write, BEQ_t, BNE, ADDI);
  or or_9 (JAL, JALR, JAL_t);
  or or_10 (J, J_t, JAL_t, JR);
  or or_11 (Write_Select, JAL, LUI);
  or or_12 (or_12_out, BEQ_t, BNE, ORI);
  or or_13 (BusW_imm, Write_Select, JALR);
  assign bit_extender_1_out = {{2{1'b0}}, or_12_out};  // Bit_Extender bit_extender_1
  nor nor_1 (nor_1_out, Rtype0001, Rtype0000);
  Multiplexer #(.width(3), .enable("false")) multiplexer_1 (
    .in0(Function), .in1(bit_extender_1_out), .out(multiplexer_1_out), .sel(nor_1_out));
  and and_1 (JR, Function[1], Function[2], Rtype0001);
  and and_2 (JALR, JR, Function[0]);
  Multiplexer #(.width(3), .enable("false")) multiplexer_2 (
    .in0(multiplexer_1_out), .in1(3'b000), .out(Function_Output), .sel(Stall));

  assign Mem_to_Reg = Mem_Read;

  // Other names for the same wires on the sheet: f0 = Function[0]; f2 = Function[1]; f1 = Function[2]; LW = Mem_Read;
  //   SW = Mem_Write
endmodule

module PC (
  input  [11:0] PC_Input,
  input  CLK,
  output [11:0] PC_Output
);

  Register #(.width(12)) PC (.D(PC_Input), .Q(PC_Output), .clk(CLK));  // open: en, clr
endmodule

module Next_PC (
  input  [11:0] Current_Instruction,
  input  clk,
  input  Reset,
  input  [5:0] Imm_6,
  input  BLTZ,
  input  Sign,
  input  BGTZ,
  input  BEQ,
  input  BNE,
  input  J,
  input  [11:0] Imm_12,
  input  Zero,
  output [11:0] Inc_PC,
  output [11:0] Next_Instruction
);

  wire and_1_out, and_2_out, and_3_out, and_4_out, not_1_out, not_2_out, or_1_out;
  wire [5:0] register_2_q;
  wire [11:0] adder_2_out, bit_extender_1_out, Next_Instrucrion_Jumps, register_1_q, register_3_q;

  Register #(.width(12)) register_1 (.D(Current_Instruction), .Q(register_1_q), .clk(clk), .clr(Reset));  // open: en
  Register #(.width(6)) register_2 (.D(Imm_6), .Q(register_2_q), .clk(clk), .clr(Reset));  // open: en
  Register #(.width(12)) register_3 (.D(register_1_q), .Q(register_3_q), .clk(clk), .clr(Reset));  // open: en
  assign bit_extender_1_out = {{6{register_2_q[5]}}, register_2_q};  // Bit_Extender bit_extender_1
  Adder #(.width(12)) adder_1 (.a(12'h1), .b(Current_Instruction), .out(Inc_PC));  // open: cin, cout
  Adder #(.width(12)) adder_2 (.a(register_3_q), .b(bit_extender_1_out), .out(adder_2_out));  // open: cin, cout
  Multiplexer #(.width(12), .enable("false")) multiplexer_1 (
    .in0(adder_2_out), .in1(Imm_12), .out(Next_Instrucrion_Jumps), .sel(J));
  and and_1 (and_1_out, BLTZ, Zero, Sign);
  or or_1 (or_1_out, J, and_1_out, and_2_out, and_3_out, and_4_out);
  not not_1 (not_1_out, Sign);
  and and_2 (and_2_out, not_1_out, Zero, BGTZ);
  and and_3 (and_3_out, BEQ, Zero);
  and and_4 (and_4_out, not_2_out, BNE);
  not not_2 (not_2_out, Zero);
  Multiplexer #(.width(12), .enable("false")) multiplexer_2 (
    .in0(Inc_PC), .in1(Next_Instrucrion_Jumps), .out(Next_Instruction), .sel(or_1_out));
endmodule

module NPC (
  input  [11:0] PC_Input,
  input  CLK,
  input  Reset,
  output [11:0] PC_Output
);

  Register #(.width(12)) PC (.D(PC_Input), .Q(PC_Output), .clk(CLK), .clr(Reset));  // open: en
endmodule

module P2 (
  input  Reset,
  input  [11:0] NPC2,
  input  [11:0] Imm,
  input  [15:0] A,
  input  [15:0] B,
  input  CLK,
  output [11:0] NPC2_2,
  output [11:0] Imm_2,
  output [15:0] A_2,
  output [15:0] B_2
);

  NPC npc_1 (.PC_Input(NPC2), .CLK(CLK), .PC_Output(NPC2_2), .Reset(Reset));
  Register #(.width(12)) register_1 (.D(Imm), .Q(Imm_2), .clk(CLK));  // open: en, clr
  Register #(.width(16)) register_2 (.D(A), .Q(A_2), .clk(CLK));  // open: en, clr
  Register #(.width(16)) register_3 (.D(B), .Q(B_2), .clk(CLK));  // open: en, clr
endmodule

module P3 (
  input  [15:0] ALU_Out,
  input  [15:0] B,
  input  CLK,
  output [15:0] ALU_Out_2,
  output [15:0] D
);

  Register #(.width(16)) register_1 (.D(ALU_Out), .Q(ALU_Out_2), .clk(CLK));  // open: en, clr
  Register #(.width(16)) register_2 (.D(B), .Q(D), .clk(CLK));  // open: en, clr
endmodule

module EX_MEM_WB (
  input  Ext_op,
  input  ALU_Src,
  input  ALU_Select,
  input  [2:0] ALU_Function,
  input  J,
  input  JR,
  input  BEQ,
  input  BNE,
  input  BLTZ,
  input  BGTZ,
  input  JAL,
  input  LUI,
  input  Write_select,
  input  BusW_imm,
  input  MEM_READ,
  input  MEM_WRITE,
  input  MEM_TO_REG,
  input  REG_WRITE,
  input  CLK,
  output Ext_op_2,
  output ALU_Src_2,
  output ALU_Select_2,
  output [2:0] ALU_Function_2,
  output J_2,
  output JR_2,
  output BEQ_2,
  output BNE_2,
  output BLTZ_2,
  output BGTZ_2,
  output JAL_2,
  output LUI_2,
  output Write_select_2,
  output BusW_imm_2,
  output Ex_Mem_Read,
  output MEM_READ_2,
  output MEM_WRITE_2,
  output MEM_TO_REG_2,
  output Reg_Write2,
  output Reg_Write3,
  output Reg_Write4,
  output REG_WRITE_2
);

  wire register_1_q, register_2_q, register_17_q, register_18_q;

  Register #(.width(1)) register_1 (.D(BusW_imm), .Q(register_1_q), .clk(CLK));  // open: en, clr
  Register #(.width(1)) register_2 (.D(register_1_q), .Q(register_2_q), .clk(CLK));  // open: en, clr
  Register #(.width(1)) register_3 (.D(register_2_q), .Q(BusW_imm_2), .clk(CLK));  // open: en, clr
  Register #(.width(1)) register_4 (.D(Ext_op), .Q(Ext_op_2), .clk(CLK));  // open: en, clr
  Register #(.width(1)) register_5 (.D(ALU_Src), .Q(ALU_Src_2), .clk(CLK));  // open: en, clr
  Register #(.width(1)) register_6 (.D(ALU_Select), .Q(ALU_Select_2), .clk(CLK));  // open: en, clr
  Register #(.width(3)) register_7 (.D(ALU_Function), .Q(ALU_Function_2), .clk(CLK));  // open: en, clr
  Register #(.width(1)) register_8 (.D(J), .Q(J_2), .clk(CLK));  // open: en, clr
  Register #(.width(1)) register_9 (.D(JR), .Q(JR_2), .clk(CLK));  // open: en, clr
  Register #(.width(1)) register_10 (.D(BEQ), .Q(BEQ_2), .clk(CLK));  // open: en, clr
  Register #(.width(1)) register_11 (.D(BNE), .Q(BNE_2), .clk(CLK));  // open: en, clr
  Register #(.width(1)) register_12 (.D(BLTZ), .Q(BLTZ_2), .clk(CLK));  // open: en, clr
  Register #(.width(1)) register_13 (.D(BGTZ), .Q(BGTZ_2), .clk(CLK));  // open: en, clr
  Register #(.width(1)) register_14 (.D(JAL), .Q(JAL_2), .clk(CLK));  // open: en, clr
  Register #(.width(1)) register_15 (.D(LUI), .Q(LUI_2), .clk(CLK));  // open: en, clr
  Register #(.width(1)) register_16 (.D(MEM_READ), .Q(Ex_Mem_Read), .clk(CLK));  // open: en, clr
  Register #(.width(1)) register_17 (.D(MEM_WRITE), .Q(register_17_q), .clk(CLK));  // open: en, clr
  Register #(.width(1)) register_18 (.D(MEM_TO_REG), .Q(register_18_q), .clk(CLK));  // open: en, clr
  Register #(.width(1)) register_19 (.D(REG_WRITE), .Q(Reg_Write2), .clk(CLK));  // open: en, clr
  Register #(.width(1)) MEM (.D(Reg_Write2), .Q(Reg_Write3), .clk(CLK));  // open: en, clr
  Register #(.width(1)) register_20 (.D(Ex_Mem_Read), .Q(MEM_READ_2), .clk(CLK));  // open: en, clr
  Register #(.width(1)) register_21 (.D(register_17_q), .Q(MEM_WRITE_2), .clk(CLK));  // open: en, clr
  Register #(.width(1)) register_22 (.D(register_18_q), .Q(MEM_TO_REG_2), .clk(CLK));  // open: en, clr
  Register #(.width(1)) WB (.D(Reg_Write3), .Q(Reg_Write4), .clk(CLK));  // open: en, clr

  assign REG_WRITE_2 = Reg_Write4;
  assign Write_select_2 = Write_select;
endmodule

// Hazard_Detect&Forwarding
module HAZARD_DETECT_AND_FORWARD (
  input  [2:0] rs,
  input  regWrite_2,
  input  regWrite_3,
  input  regWrite_4,
  input  [2:0] rd_2,
  input  [2:0] rd_3,
  input  [2:0] rd_4,
  input  Ex_Mem_Read,
  input  [2:0] rt,
  output [1:0] Forward_A,
  output Stall,
  output [1:0] Forward_B
);

  wire and_1_out, and_2_out, and_3_out, and_4_out, and_5_out, and_6_out, and_7_out, and_8_out,
       comparator_1_eq, comparator_2_eq, comparator_3_eq, comparator_4_eq, comparator_5_eq, comparator_6_eq,
       comparator_7_eq, comparator_8_eq, nor_1_out, nor_2_out, not_1_out, not_2_out, not_3_out, not_4_out,
       or_1_out;

  Comparator #(.width(3)) comparator_1 (.a(rs), .b(3'b000), .eq(comparator_1_eq));  // open: gt, lt
  Comparator #(.width(3)) comparator_2 (.a(rs), .b(rd_2), .eq(comparator_2_eq));  // open: gt, lt
  Comparator #(.width(3)) comparator_3 (.a(rs), .b(rd_3), .eq(comparator_3_eq));  // open: gt, lt
  Comparator #(.width(3)) comparator_4 (.a(rs), .b(rd_4), .eq(comparator_4_eq));  // open: gt, lt
  Comparator #(.width(3)) comparator_5 (.a(rt), .b(3'b000), .eq(comparator_5_eq));  // open: gt, lt
  Comparator #(.width(3)) comparator_6 (.a(rt), .b(rd_2), .eq(comparator_6_eq));  // open: gt, lt
  Comparator #(.width(3)) comparator_7 (.a(rt), .b(rd_3), .eq(comparator_7_eq));  // open: gt, lt
  not not_1 (not_1_out, comparator_1_eq);
  not not_2 (not_2_out, comparator_5_eq);
  Comparator #(.width(3)) comparator_8 (.a(rt), .b(rd_4), .eq(comparator_8_eq));  // open: gt, lt
  and and_1 (and_1_out, not_1_out, comparator_2_eq, regWrite_2);
  and and_2 (and_2_out, not_1_out, comparator_3_eq, regWrite_3);
  and and_3 (and_3_out, not_1_out, comparator_4_eq, regWrite_4);
  and and_4 (and_4_out, not_2_out, comparator_6_eq, regWrite_2);
  and and_5 (and_5_out, not_2_out, comparator_7_eq, regWrite_3);
  and and_6 (and_6_out, not_2_out, comparator_8_eq, regWrite_4);
  nor nor_1 (nor_1_out, and_1_out, and_2_out, and_3_out);
  Priority_Encoder #(.select(2)) priority_encoder_1 (
    .in0(nor_1_out), .in1(and_1_out), .in2(and_2_out), .in3(and_3_out), .out(Forward_A));  // open: gs, en_out, en_in
  not not_3 (not_3_out, Forward_B[1]);
  nor nor_2 (nor_2_out, and_4_out, and_5_out, and_6_out);
  Priority_Encoder #(.select(2), .disabled(0)) priority_encoder_2 (
    .in0(nor_2_out), .in1(and_4_out), .in2(and_5_out), .in3(and_6_out), .out(Forward_B));  // open: gs, en_out, en_in
  not not_4 (not_4_out, Forward_A[1]);
  and and_7 (and_7_out, not_4_out, Forward_A[0]);
  and and_8 (and_8_out, not_3_out, Forward_B[0]);
  or or_1 (or_1_out, and_7_out, and_8_out);
  and and_9 (Stall, Ex_Mem_Read, or_1_out);
endmodule

module CPU22 (
  output [15:0] t2,
  output [15:0] R1,
  output [15:0] R2,
  output [15:0] R3,
  output [15:0] R4,
  output [15:0] R5,
  output [15:0] R6,
  output [15:0] R7
);

  wire ALU_Select, ALU_Src, BEQ, BGTZ, BLTZ, BNE, BusW_imm, Clk, ex_mem_wb_1_ex_mem_read,
       ex_mem_wb_1_reg_write2, ex_mem_wb_1_reg_write3, ex_mem_wb_1_reg_write4, Ext_opr, J, JAL, JR, LUI,
       main_controller_1_alu_select, main_controller_1_alu_src, main_controller_1_beq,
       main_controller_1_bgtz, main_controller_1_bltz, main_controller_1_bne, main_controller_1_busw_imm,
       main_controller_1_ext_op, main_controller_1_j, main_controller_1_jal, main_controller_1_jr,
       main_controller_1_lui, main_controller_1_mem_read, main_controller_1_mem_to_reg,
       main_controller_1_mem_write, main_controller_1_reg_write, main_controller_1_write_select, MemRead,
       MemToReg, MemWrite, or_1_out, Reg_Dst, Reg_Write, Reset, Stall, Write_select, Zero;
  wire [1:0] F_A, F_B;
  wire [2:0] ALU_Function, Funtion, main_controller_1_function_output, multiplexer_1_out, multiplexer_2_out,
       multiplexer_3_out, rd2, rd3, rd4;
  wire [3:0] Opcode;
  wire [5:3] Imm6;
  wire [11:0] Inc_PC, multiplexer_8_out, Next_PC, P2_imm_2, PC;
  wire [11:6] Imm12;
  wire [15:0] bit_extender_1_out, bit_extender_2_out, bit_extender_3_out, BusB, BusW, F_ALU, F_MEM,
       multiplexer_4_out, multiplexer_5_out, multiplexer_6_out, multiplexer_7_out, multiplexer_9_out,
       P3_alu_out_2, P3_d, ram_1_data, RD2_2_q, RD3_2_q, RD4_2_q, register_file_1_busa, register_file_1_busb,
       rom_1_data, shifter_1_out;

  Clock clock_1 (.out(Clk));
  PC pc_1 (.PC_Input(Next_PC), .PC_Output(PC), .CLK(Clk));
  Multiplexer #(.width(3), .enable("false")) multiplexer_1 (
    .in0(Imm12[8:6]), .in1(Imm6), .out(multiplexer_1_out), .sel(Reg_Dst));
  Multiplexer #(.width(3), .enable("false")) multiplexer_2 (
    .in0(3'b001), .in1(3'b111), .out(multiplexer_2_out), .sel(JAL));
  Main_Controller main_controller_1 (
    .Reg_Dst(Reg_Dst), .Reg_Write(main_controller_1_reg_write), .Ext_Op(main_controller_1_ext_op),
    .ALU_Src(main_controller_1_alu_src), .BEQ(main_controller_1_beq), .BNE(main_controller_1_bne),
    .BGTZ(main_controller_1_bgtz), .BLTZ(main_controller_1_bltz), .J(main_controller_1_j),
    .Mem_Read(main_controller_1_mem_read), .Mem_Write(main_controller_1_mem_write),
    .Mem_to_Reg(main_controller_1_mem_to_reg), .LUI(main_controller_1_lui), .JAL(main_controller_1_jal),
    .Opcode(Opcode), .Function_Output(main_controller_1_function_output),
    .ALU_Select(main_controller_1_alu_select), .Function(Funtion), .JR(main_controller_1_jr),
    .BusW_imm(main_controller_1_busw_imm), .Write_Select(main_controller_1_write_select), .Stall(Stall));
  Register #(.width(16)) register_1 (.D(rom_1_data), .Q({Opcode, Imm12, Imm6, Funtion}), .clk(Clk));  // open: en, clr
  ROM #(.addrWidth(12), .dataWidth(16)) rom_1 (.addr(PC), .data(rom_1_data));  // open: sel
  Multiplexer #(.width(3), .enable("false")) multiplexer_3 (
    .in0(multiplexer_1_out), .in1(multiplexer_2_out), .out(multiplexer_3_out), .sel(Write_select));
  Register #(.width(3)) u_RD2 (.D(multiplexer_3_out), .Q(rd2), .clk(Clk));  // open: en, clr
  Register #(.width(3)) u_RD3 (.D(rd2), .Q(rd3), .clk(Clk));  // open: en, clr
  Register #(.width(3)) u_RD4 (.D(rd3), .Q(rd4), .clk(Clk));  // open: en, clr
  assign bit_extender_1_out = {{4{1'b0}}, {Imm12, Imm6, Funtion}};  // Bit_Extender bit_extender_1
  EX_MEM_WB ex_mem_wb_1 (
    .Ext_op(main_controller_1_ext_op), .ALU_Src(main_controller_1_alu_src),
    .ALU_Select(main_controller_1_alu_select), .ALU_Function(main_controller_1_function_output),
    .J(main_controller_1_j), .JR(main_controller_1_jr), .BEQ(main_controller_1_beq),
    .BNE(main_controller_1_bne), .BLTZ(main_controller_1_bltz), .BGTZ(main_controller_1_bgtz),
    .JAL(main_controller_1_jal), .LUI(main_controller_1_lui), .MEM_READ(main_controller_1_mem_read),
    .MEM_WRITE(main_controller_1_mem_write), .MEM_TO_REG(main_controller_1_mem_to_reg),
    .REG_WRITE(main_controller_1_reg_write), .Ext_op_2(Ext_opr), .ALU_Src_2(ALU_Src),
    .ALU_Select_2(ALU_Select), .ALU_Function_2(ALU_Function), .J_2(J), .JR_2(JR), .BEQ_2(BEQ), .BNE_2(BNE),
    .BLTZ_2(BLTZ), .BGTZ_2(BGTZ), .JAL_2(JAL), .LUI_2(LUI), .MEM_READ_2(MemRead), .MEM_WRITE_2(MemWrite),
    .MEM_TO_REG_2(MemToReg), .REG_WRITE_2(Reg_Write), .CLK(Clk), .Reg_Write2(ex_mem_wb_1_reg_write2),
    .Reg_Write3(ex_mem_wb_1_reg_write3), .Reg_Write4(ex_mem_wb_1_reg_write4),
    .Ex_Mem_Read(ex_mem_wb_1_ex_mem_read), .BusW_imm(main_controller_1_busw_imm),
    .Write_select(main_controller_1_write_select), .BusW_imm_2(BusW_imm), .Write_select_2(Write_select));
  Shifter_part #(.width(16)) shifter_1 (.in(bit_extender_1_out), .\dist (4'b0100), .out(shifter_1_out));
  assign bit_extender_2_out = {{4{1'b0}}, Inc_PC};  // Bit_Extender bit_extender_2
  Register_File register_file_1 (
    .RW(rd4), .RA(Imm12[11:9]), .RB(Imm12[8:6]), .Reg_Write(Reg_Write), .BusW(multiplexer_5_out),
    .BusA(register_file_1_busa), .BusB(register_file_1_busb), .clk(Clk), .r1(R1), .r2(R2), .r3(R3), .r4(R4),
    .r5(R5), .r6(R6), .r7(R7));
  Multiplexer #(.width(16), .enable("false")) multiplexer_4 (
    .in0(shifter_1_out), .in1(bit_extender_2_out), .out(multiplexer_4_out), .sel(JAL));
  Multiplexer #(.width(16), .enable("false")) multiplexer_5 (
    .in0(BusW), .in1(RD4_2_q), .out(multiplexer_5_out), .sel(BusW_imm));
  Register #(.width(16)) RD2_2 (.D(multiplexer_4_out), .Q(RD2_2_q), .clk(Clk));  // open: en, clr
  or or_1 (or_1_out, JAL, BGTZ, BLTZ, BNE, BEQ, JR, J);
  Multiplexer #(.select(2), .width(16), .enable("false")) multiplexer_6 (
    .in0(register_file_1_busa), .in1(F_ALU), .in2(F_MEM), .in3(BusW), .out(multiplexer_6_out), .sel(F_A));
  Multiplexer #(.select(2), .width(16), .enable("false")) multiplexer_7 (
    .in0(register_file_1_busb), .in1(F_ALU), .in2(F_MEM), .in3(BusW), .out(multiplexer_7_out), .sel(F_B));
  Register #(.width(16)) RD3_2 (.D(RD2_2_q), .Q(RD3_2_q), .clk(Clk));  // open: en, clr
  HAZARD_DETECT_AND_FORWARD hazard_detect_and_forward_1 (
    .regWrite_2(ex_mem_wb_1_reg_write2), .regWrite_3(ex_mem_wb_1_reg_write3),
    .regWrite_4(ex_mem_wb_1_reg_write4), .Forward_A(F_A), .Forward_B(F_B), .rd_2(rd2), .rd_3(rd3),
    .rd_4(rd4), .rs(Imm12[11:9]), .rt(Imm12[8:6]), .Ex_Mem_Read(ex_mem_wb_1_ex_mem_read), .Stall(Stall));
  Register #(.width(1)) register_2 (.D(or_1_out), .Q(Reset), .clk(Clk));  // open: en, clr
  Register #(.width(16)) RD4_2 (.D(RD3_2_q), .Q(RD4_2_q), .clk(Clk));  // open: en, clr
  P2 P2 (
    .Imm({Imm12, Imm6, Funtion}), .A(multiplexer_6_out), .B(multiplexer_7_out), .Reset(Reset), .CLK(Clk),
    .Imm_2(P2_imm_2), .A_2(t2), .B_2(BusB));  // open: NPC2, NPC2_2
  Multiplexer #(.width(12), .enable("false")) multiplexer_8 (
    .in0(P2_imm_2), .in1(t2[11:0]), .out(multiplexer_8_out), .sel(JR));
  assign bit_extender_3_out = {{10{P2_imm_2[5]}}, P2_imm_2[5:0]};  // Bit_Extender bit_extender_3
  Multiplexer #(.width(16), .enable("false")) multiplexer_9 (
    .in0(BusB), .in1(bit_extender_3_out), .out(multiplexer_9_out), .sel(ALU_Src));
  Next_PC next_pc_1 (
    .BLTZ(BLTZ), .Sign(t2[15]), .Zero(Zero), .BGTZ(BGTZ), .BEQ(BEQ), .BNE(BNE), .Next_Instruction(Next_PC),
    .Current_Instruction(PC), .J(J), .Imm_12(multiplexer_8_out), .Imm_6({Imm6, Funtion}), .Reset(Reset),
    .clk(Clk));  // open: Inc_PC
  ALU alu_1 (
    .ALU_Function(ALU_Function), .ALU_Output(F_ALU), .A(t2), .B(multiplexer_9_out), .ALU_Select(ALU_Select),
    .ZERO(Zero));
  P3 P3 (.ALU_Out(F_ALU), .B(BusB), .CLK(Clk), .ALU_Out_2(P3_alu_out_2), .D(P3_d));
  RAM #(.addrWidth(12), .dataWidth(16), .bus("separate")) ram_1 (
    .addr(P3_alu_out_2[11:0]), .din(P3_d), .data(ram_1_data), .str(MemWrite), .clk(Clk), .ld(MemRead));  // open: sel, clr
  Multiplexer #(.width(16), .enable("false")) multiplexer_10 (
    .in0(P3_alu_out_2), .in1(ram_1_data), .out(F_MEM), .sel(MemToReg));
  Register #(.width(16)) register_3 (.D(F_MEM), .Q(BusW), .clk(Clk));  // open: en, clr

  // Other names for the same wires on the sheet: Imm6[2:0] = Funtion; Imm12[5:0] = {Imm6, Funtion}; Rd[2:0] = Imm6;
  //   Rt[2:0] = Imm12[8:6]; Rs[2:0] = Imm12[11:9]; BusA[15:0] = t2; Sign = t2[15]

  // Notes on the sheet:
  //   contents of rom_1 (hex, n*v repeats v):
  //   b003 a005
endmodule
