// Logisim project Single_Cycle_Procesessor.circ as structural Verilog
// Regiser_File
module Register_File (
  input  [2:0] RA,
  input  [2:0] RB,
  input  [2:0] RW,
  input  [15:0] BusW,
  input  Reg_Write,
  output [15:0] BusA,
  output [15:0] BusB
);

  wire A_D0, A_D1, A_D2, A_D3, A_D4, A_D5, A_D6, A_D7, and_1_out, and_2_out, and_3_out, and_4_out, and_5_out,
       and_6_out, and_7_out, B_D0, B_D1, B_D2, B_D3, B_D4, B_D5, B_D6, B_D7, clk, R1_Enable, R2_Enable,
       R3_Enable, R4_Enable, R5_Enable, R6_Enable, R7_Enable;
  wire [15:0] R1_2_q, R1_q, R2_q, R3_q, R4_q, R5_q, R6_q, R7_q;

  Decoder #(.select(3), .enable("false")) decoder_1 (
    .out0(A_D0), .out1(A_D1), .out2(A_D2), .out3(A_D3), .out4(A_D4), .out5(A_D5), .out6(A_D6), .out7(A_D7),
    .sel(RA));
  Decoder #(.select(3), .enable("false")) decoder_2 (
    .out0(B_D0), .out1(B_D1), .out2(B_D2), .out3(B_D3), .out4(B_D4), .out5(B_D5), .out6(B_D6), .out7(B_D7),
    .sel(RB));
  Decoder #(.select(3), .enable("false")) decoder_3 (
    .out1(R1_Enable), .out2(R2_Enable), .out3(R3_Enable), .out4(R4_Enable), .out5(R5_Enable),
    .out6(R6_Enable), .out7(R7_Enable), .sel(RW));  // open: out0
  Clock clock_1 (.out(clk));
  and and_1 (and_1_out, Reg_Write, R1_Enable);
  and and_2 (and_2_out, Reg_Write, R2_Enable);
  and and_3 (and_3_out, Reg_Write, R3_Enable);
  and and_4 (and_4_out, Reg_Write, R4_Enable);
  and and_5 (and_5_out, Reg_Write, R5_Enable);
  and and_6 (and_6_out, Reg_Write, R6_Enable);
  and and_7 (and_7_out, Reg_Write, R7_Enable);
  Register #(.width(16)) R1 (.D({16{1'b0}}), .Q(R1_q), .clr(clk));  // open: en, clk
  Register #(.width(16)) R1_2 (.D(BusW), .Q(R1_2_q), .clk(and_1_out), .clr(clk));  // open: en
  Register #(.width(16)) R2 (.D(BusW), .Q(R2_q), .clk(and_2_out), .clr(clk));  // open: en
  Register #(.width(16)) R3 (.D(BusW), .Q(R3_q), .clk(and_3_out), .clr(clk));  // open: en
  Register #(.width(16)) R4 (.D(BusW), .Q(R4_q), .clk(and_4_out), .clr(clk));  // open: en
  Register #(.width(16)) R5 (.D(BusW), .Q(R5_q), .clk(and_5_out), .clr(clk));  // open: en
  Register #(.width(16)) R6 (.D(BusW), .Q(R6_q), .clk(and_6_out), .clr(clk));  // open: en
  Register #(.width(16)) R7 (.D(BusW), .Q(R7_q), .clk(and_7_out), .clr(clk));  // open: en
  assign BusB = B_D0 ? R1_q : 16'bz;  // Controlled_Buffer controlled_buffer_1
  assign BusB = B_D1 ? R1_2_q : 16'bz;  // Controlled_Buffer controlled_buffer_2
  assign BusB = B_D2 ? R2_q : 16'bz;  // Controlled_Buffer controlled_buffer_3
  assign BusB = B_D3 ? R3_q : 16'bz;  // Controlled_Buffer controlled_buffer_4
  assign BusB = B_D4 ? R4_q : 16'bz;  // Controlled_Buffer controlled_buffer_5
  assign BusB = B_D5 ? R5_q : 16'bz;  // Controlled_Buffer controlled_buffer_6
  assign BusB = B_D6 ? R6_q : 16'bz;  // Controlled_Buffer controlled_buffer_7
  assign BusB = B_D7 ? R7_q : 16'bz;  // Controlled_Buffer controlled_buffer_8
  assign BusA = A_D0 ? R1_q : 16'bz;  // Controlled_Buffer controlled_buffer_9
  assign BusA = A_D1 ? R1_2_q : 16'bz;  // Controlled_Buffer controlled_buffer_10
  assign BusA = A_D2 ? R2_q : 16'bz;  // Controlled_Buffer controlled_buffer_11
  assign BusA = A_D3 ? R3_q : 16'bz;  // Controlled_Buffer controlled_buffer_12
  assign BusA = A_D4 ? R4_q : 16'bz;  // Controlled_Buffer controlled_buffer_13
  assign BusA = A_D5 ? R5_q : 16'bz;  // Controlled_Buffer controlled_buffer_14
  assign BusA = A_D6 ? R6_q : 16'bz;  // Controlled_Buffer controlled_buffer_15
  assign BusA = A_D7 ? R7_q : 16'bz;  // Controlled_Buffer controlled_buffer_16
endmodule

module ALU (
  input  [15:0] A,
  input  [15:0] B,
  input  [2:0] ALU_Function,
  input  Opcode0_1_Select,
  output [15:0] ALU_Output
);

  wire [15:0] au_1_arithmetic_output, lu_and_shifter_1_opcode0_output;

  LU_and_Shifter lu_and_shifter_1 (
    .Opcode0_Output(lu_and_shifter_1_opcode0_output), .A(A), .B(B), .Opcode0_Select(ALU_Function));
  AU au_1 (.Arithmetic_Output(au_1_arithmetic_output), .A(A), .B(B), .Arithmetic_Select(ALU_Function));
  Multiplexer #(.width(16), .enable("false")) multiplexer_1 (
    .in0(lu_and_shifter_1_opcode0_output), .in1(au_1_arithmetic_output), .out(ALU_Output),
    .sel(Opcode0_1_Select));
endmodule

module Logical_Unit (
  input  [15:0] A,
  input  [15:0] B,
  output [15:0] AND_Output,
  output [15:0] OR_Output,
  output [15:0] NOR_Output,
  output [15:0] XOR_Output
);

  assign AND_Output = B & A;  // AND_Gate AND, 16 bits wide
  assign OR_Output = B | A;  // OR_Gate OR, 16 bits wide
  assign XOR_Output = B ^ A;  // XOR_Gate XOR, 16 bits wide
  assign NOR_Output = ~OR_Output;  // NOT_Gate not_1, 16 bits wide
endmodule

module Shifter (
  input  [3:0] Shift_Amount,
  input  [15:0] Number,
  output [15:0] SLL_Outout,
  output [15:0] SRL_Outout,
  output [15:0] SRA_Outout,
  output [15:0] ROL_Outout
);

  Shifter_part #(.width(16)) shifter_1 (.in(Number), .\dist (Shift_Amount), .out(SLL_Outout));
  Shifter_part #(.width(16), .shift("lr")) shifter_2 (.in(Number), .\dist (Shift_Amount), .out(SRL_Outout));
  Shifter_part #(.width(16), .shift("ar")) shifter_3 (.in(Number), .\dist (Shift_Amount), .out(SRA_Outout));
  Shifter_part #(.width(16), .shift("rl")) shifter_4 (.in(Number), .\dist (Shift_Amount), .out(ROL_Outout));
endmodule

module AU (
  input  [15:0] A,
  input  [15:0] B,
  input  [2:0] Arithmetic_Select,
  output [15:0] Arithmetic_Output
);

  wire subtractor_1_bout, subtractor_2_bout, xor_1_out;
  wire [15:0] Add_Output, Different_sign_Comp, nor_1_out, or_1_out, or_2_out, SLT, SLTE, SLTEU, SLTU,
       Sub_Output;

  xor xor_1 (xor_1_out, A[15], B[15]);
  Adder #(.width(16)) adder_1 (.a(A), .b(B), .out(Add_Output));  // open: cin, cout
  Subtractor #(.width(16)) subtractor_1 (.a(A), .b(B), .out(Sub_Output), .bout(subtractor_1_bout));  // open: bin
  Subtractor #(.width(1)) subtractor_2 (.a(B[15]), .b(A[15]), .bout(subtractor_2_bout));  // open: out, bin
  assign SLTU = {{15{1'b0}}, subtractor_1_bout};  // Bit_Extender bit_extender_1
  Multiplexer #(.width(16), .enable("false")) multiplexer_1 (
    .in0(SLTU), .in1(Different_sign_Comp), .out(SLT), .sel(xor_1_out));
  assign Different_sign_Comp = {{15{1'b0}}, subtractor_2_bout};  // Bit_Extender bit_extender_2
  assign nor_1_out = ~({16{1'b0}} | Sub_Output);  // NOR_Gate nor_1, 16 bits wide
  assign or_1_out = SLTU | nor_1_out;  // OR_Gate or_1, 16 bits wide
  assign or_2_out = nor_1_out | SLT;  // OR_Gate or_2, 16 bits wide
  assign SLTEU = {{15{1'b0}}, or_1_out[0]};  // Bit_Extender bit_extender_3
  assign SLTE = {{15{1'b0}}, or_2_out[0]};  // Bit_Extender bit_extender_4
  Multiplexer #(.select(3), .width(16), .enable("false")) multiplexer_2 (
    .in0(Add_Output), .in1(Sub_Output), .in2(SLT), .in3(SLTU), .in4(SLTE), .in5(SLTEU),
    .out(Arithmetic_Output), .sel(Arithmetic_Select));  // open: in6, in7
endmodule

// LU&Shifter
module LU_and_Shifter (
  input  [15:0] A,
  input  [15:0] B,
  input  [2:0] Opcode0_Select,
  output [15:0] Opcode0_Output
);

  wire [15:0] logical_unit_1_and_output, logical_unit_1_nor_output, logical_unit_1_or_output,
       logical_unit_1_xor_output, shifter_1_rol_outout, shifter_1_sll_outout, shifter_1_sra_outout,
       shifter_1_srl_outout;

  Logical_Unit logical_unit_1 (
    .B(B), .A(A), .AND_Output(logical_unit_1_and_output), .OR_Output(logical_unit_1_or_output),
    .NOR_Output(logical_unit_1_nor_output), .XOR_Output(logical_unit_1_xor_output));
  Shifter shifter_1 (
    .Shift_Amount(A[3:0]), .Number(B), .SLL_Outout(shifter_1_sll_outout), .SRL_Outout(shifter_1_srl_outout),
    .SRA_Outout(shifter_1_sra_outout), .ROL_Outout(shifter_1_rol_outout));
  Multiplexer #(.select(3), .width(16), .enable("false")) multiplexer_1 (
    .in0(logical_unit_1_and_output), .in1(logical_unit_1_or_output), .in2(logical_unit_1_xor_output),
    .in3(logical_unit_1_nor_output), .in4(shifter_1_sll_outout), .in5(shifter_1_srl_outout),
    .in6(shifter_1_sra_outout), .in7(shifter_1_rol_outout), .out(Opcode0_Output), .sel(Opcode0_Select));
endmodule

module Single_Cycle_Processor (
);

  wire [2:0] Funtion, multiplexer_1_out, Rd, Rs, Rt;
  wire [3:0] Opcode;
  wire [11:0] pc_1_pc_output;
  wire [15:0] bit_extender_1_out, multiplexer_2_out, register_file_1_busa, register_file_1_busb;

  PC pc_1 (.PC_Output(pc_1_pc_output));  // open: PC_Input
  ROM #(.addrWidth(12), .dataWidth(16)) rom_1 (
    .addr(pc_1_pc_output), .data({Opcode, Rs, Rt, Rd, Funtion}));  // open: sel
  Main_Controller main_controller_1 ();  // open: Instruction_Input, Reg_Dst, Reg_Write, Ext_Op, ALU_Src, BEQ, BNE, BGTZ, BLTZ, J, Mem_Read, Mem_Write, Mem_to_Reg, Function_Code_Output, ALU_Control
  Multiplexer #(.width(3), .enable("false")) multiplexer_1 (.in0(Rt), .in1(Rd), .out(multiplexer_1_out));  // open: sel
  Register_File register_file_1 (
    .RW(multiplexer_1_out), .RA(Rs), .RB(Rt), .BusA(register_file_1_busa), .BusB(register_file_1_busb));  // open: Reg_Write, BusW
  assign bit_extender_1_out = {{10{1'b0}}, {Funtion, Rd}};  // Bit_Extender bit_extender_1
  Multiplexer #(.width(16), .enable("false")) multiplexer_2 (
    .in0(register_file_1_busb), .in1(bit_extender_1_out), .out(multiplexer_2_out));  // open: sel
  Next_PC next_pc_1 ();  // open: Current_Instruction, Immediate, Jump, BLTEZ, SLTE, BGEZ, BEQ, Zero, BNE, BLTZ, SLT, BGTZ, Next_Instrucrion
  ALU alu_1 (.A(register_file_1_busa), .B(multiplexer_2_out));  // open: ALU_Function, ALU_Output, Opcode0_1_Select
  RAM ram_1 ();  // open: addr, data, sel, clk, ld, clr
endmodule

module Main_Controller (
  input  [15:0] Instruction_Input,
  output [2:0] Function_Code_Output,
  output ALU_Control,
  output Reg_Dst,
  output Reg_Write,
  output Ext_Op,
  output ALU_Src,
  output BEQ,
  output BNE,
  output BGTZ,
  output BLTZ,
  output J,
  output Mem_Read,
  output Mem_Write,
  output Mem_to_Reg
);

  wire ADDI, ANDI, BEQ_t, BGEZ, BGTZ_t, BLEZ, BLTZ_t, J_t, JAL, LUI, nor_1_out, nor_2_out, ORI, Rtype0000,
       Rtype0001;
  wire [2:0] bit_extender_1_out;

  Decoder #(.select(4), .enable("false")) decoder_1 (
    .out0(Rtype0000), .out1(Rtype0001), .out2(Mem_Read), .out3(Mem_Write), .out4(BEQ_t), .out5(BNE),
    .out6(ANDI), .out7(ORI), .out8(ADDI), .out9(J_t), .out10(JAL), .out11(LUI), .out12(BLTZ_t), .out13(BLEZ),
    .out14(BGTZ_t), .out15(BGEZ), .sel(Instruction_Input[15:12]));
  or or_1 (Reg_Dst, Rtype0000, Rtype0001);
  or or_2 (Reg_Write, Rtype0000, Rtype0001, Mem_Read, ANDI, ORI, ADDI, LUI);
  or or_3 (ALU_Src, Mem_Read, BEQ_t, ANDI, ORI, ADDI);
  or or_4 (Ext_Op, Mem_Read, Mem_Write, ADDI, LUI);
  or or_5 (BEQ, BEQ_t, BLEZ, BGTZ_t);
  or or_6 (BGTZ, BLEZ, BGEZ);
  or or_7 (BLTZ, BLTZ_t, BGTZ_t);
  or or_8 (J, J_t, JAL);
  nor nor_1 (nor_1_out, Rtype0000, Rtype0001);
  nor nor_2 (nor_2_out, Mem_Read, Mem_Write, ANDI, ADDI);
  Multiplexer #(.width(3), .enable("false")) multiplexer_1 (
    .in0(Instruction_Input[2:0]), .in1(bit_extender_1_out), .out(Function_Code_Output), .sel(nor_1_out));
  assign bit_extender_1_out = {{2{1'b0}}, nor_2_out};  // Bit_Extender bit_extender_1
  nor nor_3 (ALU_Control, Rtype0000, ORI, ANDI);

  assign Mem_to_Reg = Mem_Read;

  // Other names for the same wires on the sheet: Fuction_Code[2:0] = Instruction_Input[2:0];
  //   Opcode[3:0] = Instruction_Input[15:12]; LW = Mem_Read; SW = Mem_Write
endmodule

module PC (
  input  [11:0] PC_Input,
  output [11:0] PC_Output
);

  wire clock_1_out;

  Clock clock_1 (.out(clock_1_out));
  Register #(.width(12)) PC (.D(PC_Input), .Q(PC_Output), .clk(clock_1_out));  // open: en, clr
endmodule

module Next_PC (
  input  [11:0] Current_Instruction,
  input  [11:0] Immediate,
  input  Jump,
  input  BEQ,
  input  BNE,
  input  BLTZ,
  input  SLT,
  input  BGTZ,
  input  BLTEZ,
  input  SLTE,
  input  BGEZ,
  input  Zero,
  output [11:0] Next_Instrucrion
);

  wire and_1_out, and_2_out, and_3_out, and_4_out, and_5_out, and_6_out, not_1_out, not_2_out, not_3_out,
       undriven;
  wire [11:0] adder_1_out;

  ALU_Controller alu_controller_1 ();
  Adder #(.width(12)) adder_1 (.a(Current_Instruction), .b(12'h1), .out(adder_1_out));  // open: cin, cout
  Multiplexer #(.width(12), .enable("false")) multiplexer_1 (
    .in0(adder_1_out), .in1(Immediate), .out(Next_Instrucrion), .sel(undriven));
  and and_1 (and_1_out, BLTEZ, SLTE);
  and and_2 (and_2_out, not_1_out, BGEZ);
  not not_1 (not_1_out, SLTE);
  and and_3 (and_3_out, BEQ, Zero);
  and and_4 (and_4_out, not_2_out, BNE);
  not not_2 (not_2_out, Zero);
  and and_5 (and_5_out, BLTZ, SLT);
  and and_6 (and_6_out, not_3_out, BGTZ);
  not not_3 (not_3_out, SLT);
endmodule
